// Logisim project 3_bits.circ as structural Verilog
module test (
  input  in_1,
  input  in_2,
  input  in_3,
  input  [7:0] in_4,
  input  [7:0] in_5,
  input  [3:0] in_6,
  input  [3:0] in_7,
  input  [3:0] in_8,
  input  [3:0] in_9,
  input  [1:0] in_10,
  input  [1:0] in_11,
  output out_12,
  output out_13,
  output out_14,
  output out_15,
  output [7:0] out_16,
  output [3:0] out_17,
  output [3:0] out_18,
  output [3:0] out_19,
  output [3:0] out_20
);

  wire and_2_out, and_3_out, and_4_out, and_5_out, and_6_out, and_7_out, and_8_out, and_9_out, and_10_out,
       and_11_out, and_12_out, and_13_out, not_1_out, not_2_out, not_3_out, not_4_out, not_6_out, not_7_out,
       not_8_out, not_9_out, not_10_out, not_11_out, not_12_out, not_13_out, not_14_out, not_16_out,
       not_17_out, not_18_out, not_19_out;

  not not_1 (not_1_out, in_2);
  not not_2 (not_2_out, in_1);
  and and_1 (out_13, in_1, in_2);
  and and_2 (and_2_out, not_1_out, in_1);
  and and_3 (and_3_out, in_2, not_2_out);
  Adder adder_1 (.a(in_4), .b(in_5), .out(out_16));  // open: cin, cout
  not not_3 (not_3_out, and_2_out);
  not not_4 (not_4_out, and_3_out);
  // Probe on out_16
  and and_4 (and_4_out, not_3_out, not_4_out);
  not not_5 (out_14, and_4_out);
  not not_6 (not_6_out, in_1);
  not not_7 (not_7_out, in_2);
  not not_8 (not_8_out, in_1);
  not not_9 (not_9_out, in_3);
  not not_10 (not_10_out, in_2);
  not not_11 (not_11_out, in_3);
  Multiplexer #(.select(2), .width(4)) multiplexer_1 (
    .in0(in_6), .in1(in_7), .in2(in_8), .in3(in_9), .sel(in_10));  // open: out, en
  and and_5 (and_5_out, in_2, in_3);
  and and_6 (and_6_out, in_1, in_2);
  and and_7 (and_7_out, in_1, in_3);
  and and_8 (and_8_out, not_6_out, not_7_out, in_3);
  and and_9 (and_9_out, not_8_out, in_2, not_9_out);
  and and_10 (and_10_out, in_1, in_2, in_3);
  and and_11 (and_11_out, in_1, not_10_out, not_11_out);
  Demultiplexer #(.select(2), .width(4)) demultiplexer_1 (
    .out0(out_17), .out1(out_18), .out2(out_19), .out3(out_20), .sel(in_11));  // open: in, en
  not not_12 (not_12_out, and_5_out);
  not not_13 (not_13_out, and_6_out);
  not not_14 (not_14_out, and_7_out);
  and and_12 (and_12_out, not_12_out, not_13_out, not_14_out);
  not not_15 (out_12, and_12_out);
  not not_16 (not_16_out, and_8_out);
  not not_17 (not_17_out, and_9_out);
  and and_13 (and_13_out, not_16_out, not_17_out, not_18_out, not_19_out);
  not not_18 (not_18_out, and_10_out);
  not not_19 (not_19_out, and_11_out);
  not not_20 (out_15, and_13_out);

  // Other names for the same wires on the sheet: A = in_1; B = in_2; C = in_3
endmodule

module calc (
  input  [7:0] in_1,
  input  [7:0] in_2,
  input  [1:0] in_3
);

  wire R;
  wire [7:0] A_minus, A_plus, A_star, A_t, adder_1_out, B_minus, B_plus, B_star, B_t, divider_1_out,
       multiplexer_1_out, multiplier_1_out, register_1_q, subtractor_1_out;

  Button button (.out(R));
  // Probe on in_1
  // Probe on in_2
  Adder adder_1 (.a(A_plus), .b(B_plus), .out(adder_1_out));  // open: cin, cout
  Subtractor subtractor_1 (.a(A_minus), .b(B_minus), .out(subtractor_1_out));  // open: bin, bout
  Multiplier multiplier_1 (.a(A_star), .b(B_star), .out(multiplier_1_out));  // open: cin, cout
  Divider divider_1 (.a(A_t), .b(B_t), .out(divider_1_out));  // open: upper, rem
  Demultiplexer #(.select(2), .width(8)) demultiplexer_1 (
    .out0(A_plus), .out1(A_minus), .out2(A_star), .out3(A_t), .in(in_1), .sel(in_3), .en(R));
  Demultiplexer #(.select(2), .width(8)) demultiplexer_2 (
    .out0(B_plus), .out1(B_minus), .out2(B_star), .out3(B_t), .in(in_2), .sel(in_3), .en(R));
  Multiplexer #(.select(2), .width(8)) multiplexer_1 (
    .in0(adder_1_out), .in1(subtractor_1_out), .in2(multiplier_1_out), .in3(divider_1_out),
    .out(multiplexer_1_out), .sel(in_3), .en(R));
  Register #(.trigger("high")) register_1 (.D(multiplexer_1_out), .en(R), .Q(register_1_q), .clk(R));  // open: clr
  // Probe on register_1_q

  // Other names for the same wires on the sheet: A[7:0] = in_1; B[7:0] = in_2; O[1:0] = in_3
endmodule

module sus (
  input  [15:0] in_1,
  input  [15:0] in_2,
  input  [3:0] in_3,
  output [15:0] out_4
);

  wire comparator_1_eq, comparator_1_gt, comparator_1_lt, R;
  wire [15:0] AND, ANEGATIVE, DIV, EQUAL, GREATER, LEFTSHIFT, LESS, MULT, multiplexer_1_out, NOT, OR,
       RIGHTSHIFT, SUB, SUM, XOR;

  Button button (.out(R));
  // Probe on in_1
  // Probe on in_2
  Multiplexer #(.select(4), .width(16)) multiplexer_1 (
    .in0(SUM), .in1(SUB), .in2(MULT), .in3(DIV), .in4(AND), .in5(OR), .in6(XOR), .in7(NOT), .in8(LESS),
    .in9(EQUAL), .in10(GREATER), .in11(LEFTSHIFT), .in12(RIGHTSHIFT), .in13(ANEGATIVE),
    .out(multiplexer_1_out), .sel(in_3), .en(R));  // open: in14, in15
  // Probe on out_4
  Register #(.width(16), .trigger("high")) register_1 (.D(multiplexer_1_out), .en(R), .Q(out_4), .clk(R));  // open: clr
  RAM ram_1 ();  // open: addr, data, sel, clk, ld, clr
  Adder #(.width(16)) adder_1 (.a(in_1), .b(in_2), .out(SUM));  // open: cin, cout
  Subtractor #(.width(16)) subtractor_1 (.a(in_1), .b(in_2), .out(SUB));  // open: bin, bout
  Multiplier #(.width(16)) multiplier_1 (.a(in_1), .b(in_2), .out(MULT));  // open: cin, cout
  Divider #(.width(16)) divider_1 (.a(in_1), .b(in_2), .out(DIV));  // open: upper, rem
  assign AND = in_1 & in_2;  // AND_Gate and_1, 16 bits wide
  assign OR = in_1 | in_2;  // OR_Gate or_1, 16 bits wide
  assign XOR = in_1 ^ in_2;  // XOR_Gate xor_1, 16 bits wide
  assign NOT = ~in_1;  // NOT_Gate not_1, 16 bits wide
  assign GREATER = {{15{1'b0}}, comparator_1_gt};  // Bit_Extender bit_extender_1
  assign EQUAL = {{15{1'b0}}, comparator_1_eq};  // Bit_Extender bit_extender_2
  Comparator #(.width(16)) comparator_1 (
    .a(in_1), .b(in_2), .gt(comparator_1_gt), .eq(comparator_1_eq), .lt(comparator_1_lt));
  assign LESS = {{15{1'b0}}, comparator_1_lt};  // Bit_Extender bit_extender_3
  Shifter #(.width(16)) shifter_1 (.in(in_1), .\dist (in_2[3:0]), .out(LEFTSHIFT));
  Shifter #(.width(16), .shift("lr")) shifter_2 (.in(in_1), .\dist (in_2[3:0]), .out(RIGHTSHIFT));
  Negator #(.width(16)) negator_1 (.in(in_1), .out(ANEGATIVE));

  // Other names for the same wires on the sheet: A[15:0] = in_1; B[15:0] = in_2; O[3:0] = in_3
endmodule

module flipflop (
  input  Dale,
  input  Enable,
  output out_3
);

  wire and_1_out, and_2_out, not_1_out, not_2_out, not_3_out;

  not not_1 (not_1_out, and_1_out);
  and and_1 (and_1_out, Dale, Enable);
  not not_2 (not_2_out, and_2_out);
  and and_2 (and_2_out, Enable, not_3_out);
  not not_3 (not_3_out, Dale);
  LSR lsr_1 (.Set(not_1_out), .Reset(not_2_out), .out_3(out_3));
endmodule

module LSR (
  input  Set,
  input  Reset,
  output out_3
);

  wire and_1_out, and_2_out, not_2_out;

  not not_1 (out_3, and_1_out);
  and and_1 (and_1_out, Set, not_2_out);
  not not_2 (not_2_out, and_2_out);
  and and_2 (and_2_out, out_3, Reset);
endmodule
