// Logisim project proce.circ as structural Verilog
module Processador (
  input  [15:0] in_1
);
endmodule

module registradores (
  input  in_1,
  input  in_2,
  input  in_3,
  input  [3:0] in_4,
  input  [3:0] in_5,
  input  [15:0] in_6,
  output [15:0] out_7,
  output [15:0] out_8
);

  wire E1, E2, E3, E4, E5, E6, E7, E8, E9, E10, E11, E12, E13, E14, E15, E16;
  wire [15:0] ES1, ES2, ES3, ES4, ES5, ES6, ES7, ES8, ES9, ES10, ES11, ES12, ES13, ES14, ES15, ES16;

  Register #(.width(16)) register_1 (.D(in_6), .en(E1), .Q(ES1), .clk(in_1), .clr(in_2));
  Register #(.width(16)) register_2 (.D(in_6), .en(E2), .Q(ES2), .clk(in_1), .clr(in_2));
  Register #(.width(16)) register_3 (.D(in_6), .en(E3), .Q(ES3), .clk(in_1), .clr(in_2));
  Register #(.width(16)) register_4 (.D(in_6), .en(E4), .Q(ES4), .clk(in_1), .clr(in_2));
  Register #(.width(16)) register_5 (.D(in_6), .en(E5), .Q(ES5), .clk(in_1), .clr(in_2));
  Demultiplexer #(.select(4), .enable("false")) demultiplexer_1 (
    .out0(E1), .out1(E2), .out2(E3), .out3(E4), .out4(E5), .out5(E6), .out6(E7), .out7(E8), .out8(E9),
    .out9(E10), .out10(E11), .out11(E12), .out12(E13), .out13(E14), .out14(E15), .out15(E16), .in(in_3),
    .sel(in_5));
  Register #(.width(16)) register_6 (.D(in_6), .en(E6), .Q(ES6), .clk(in_1), .clr(in_2));
  Register #(.width(16)) register_7 (.D(in_6), .en(E7), .Q(ES7), .clk(in_1), .clr(in_2));
  Register #(.width(16)) register_8 (.D(in_6), .en(E8), .Q(ES8), .clk(in_1), .clr(in_2));
  Register #(.width(16)) register_9 (.D(in_6), .en(E9), .Q(ES9), .clk(in_1), .clr(in_2));
  Multiplexer #(.select(4), .width(16), .enable("false")) multiplexer_1 (
    .in0(ES1), .in1(ES2), .in2(ES3), .in3(ES4), .in4(ES5), .in5(ES6), .in6(ES7), .in7(ES8), .in8(ES9),
    .in9(ES10), .in10(ES11), .in11(ES12), .in12(ES13), .in13(ES14), .in14(ES15), .in15(ES16), .out(out_7),
    .sel(in_4));
  Multiplexer #(.select(4), .width(16), .enable("false")) multiplexer_2 (
    .in0(ES1), .in1(ES2), .in2(ES3), .in3(ES4), .in4(ES5), .in5(ES6), .in6(ES7), .in7(ES8), .in8(ES9),
    .in9(ES10), .in10(ES11), .in11(ES12), .in12(ES13), .in13(ES14), .in14(ES15), .in15(ES16), .out(out_8),
    .sel(in_5));
  Register #(.width(16)) register_10 (.D(in_6), .en(E10), .Q(ES10), .clk(in_1), .clr(in_2));
  Register #(.width(16)) register_11 (.D(in_6), .en(E11), .Q(ES11), .clk(in_1), .clr(in_2));
  Register #(.width(16)) register_12 (.D(in_6), .en(E12), .Q(ES12), .clk(in_1), .clr(in_2));
  Register #(.width(16)) register_13 (.D(in_6), .en(E13), .Q(ES13), .clk(in_1), .clr(in_2));
  Register #(.width(16)) register_14 (.D(in_6), .en(E14), .Q(ES14), .clk(in_1), .clr(in_2));
  Register #(.width(16)) register_15 (.D(in_6), .en(E15), .Q(ES15), .clk(in_1), .clr(in_2));
  Register #(.width(16)) register_16 (.D(in_6), .en(E16), .Q(ES16), .clk(in_1), .clr(in_2));

  // Other names for the same wires on the sheet: Cl = in_1; Data[15:0] = in_6; En = in_3; GET[3:0] = in_4; RST = in_2;
  //   SET[3:0] = in_5

  // Notes on the sheet:
  //   6577
endmodule
