// Logisim project aula-03.circ as structural Verilog
module LSR (
  input  Set,
  input  Reset,
  output out_3
);

  wire and_1_out, and_2_out, not_2_out;

  and and_1 (and_1_out, Set, not_2_out);
  not not_1 (out_3, and_1_out);
  not not_2 (not_2_out, and_2_out);
  and and_2 (and_2_out, out_3, Reset);
endmodule

// LD
module LatchD (
  input  Data,
  input  Enable,
  output out_3
);

  wire and_1_out, and_2_out, not_1_out, not_2_out, not_3_out;

  not not_1 (not_1_out, and_1_out);
  and and_1 (and_1_out, Data, Enable);
  not not_2 (not_2_out, and_2_out);
  and and_2 (and_2_out, Enable, not_3_out);
  not not_3 (not_3_out, Data);
  LSR lsr_1 (.Set(not_1_out), .Reset(not_2_out), .out_3(out_3));
endmodule

module flipflop (
  input  Data,
  input  Enable,
  input  Clock,
  output out_4
);

  wire and_1_out, latchd_1_out_3, not_1_out;

  LatchD latchd_1 (.Data(Data), .Enable(and_1_out), .out_3(latchd_1_out_3));
  and and_1 (and_1_out, Enable, Clock);
  not not_1 (not_1_out, Clock);
  LatchD latchd_2 (.Data(latchd_1_out_3), .Enable(not_1_out), .out_3(out_4));
endmodule

module clock (
  input  Data,
  input  Data_2,
  output out_3
);

  wire and_1_out, Clock_out, flipflop_1_out_4, not_1_out;

  Clock Clock (.out(Clock_out));
  Clock Clock_2 ();  // open: out
  not not_1 (not_1_out, flipflop_1_out_4);
  flipflop flipflop_1 (.Data(Data), .Enable(1'b1), .Clock(Clock_out), .out_4(flipflop_1_out_4));
  and and_1 (and_1_out, Data, not_1_out);
  flipflop flipflop_2 (.Data(and_1_out), .Enable(1'b1), .Clock(Clock_out), .out_4(out_3));
endmodule

module atv_01 (
  input  [3:0] in_1,
  input  [1:0] in_2,
  input  [1:0] in_3,
  input  [1:0] in_4,
  output [3:0] out_5,
  output [3:0] out_6
);

  wire CLK, ON1, ON2, ON3, RST, RST1, RST2, RST3, SET;
  wire [3:0] OUT1, OUT2, OUT3;

  Button button_1 (.out(SET));
  // Probe on out_5
  Button button_2 (.out(RST));
  // Probe on out_6
  Register #(.width(4)) register_1 (.D(in_1), .en(ON1), .Q(OUT1), .clk(CLK), .clr(RST1));
  Demultiplexer #(.select(2), .enable("false")) demultiplexer_1 (
    .out1(ON1), .out2(ON2), .out3(ON3), .in(SET), .sel(in_2));  // open: out0
  Multiplexer #(.select(2), .width(4), .enable("false")) multiplexer_1 (
    .in1(OUT1), .in2(OUT2), .in3(OUT3), .out(out_5), .sel(in_2));  // open: in0
  Register #(.width(4)) register_2 (.D(in_1), .en(ON2), .Q(OUT2), .clk(CLK), .clr(RST2));
  Demultiplexer #(.select(2), .enable("false")) demultiplexer_2 (
    .out1(RST1), .out2(RST2), .out3(RST3), .in(RST), .sel(in_4));  // open: out0
  Multiplexer #(.select(2), .width(4), .enable("false")) multiplexer_2 (
    .in1(OUT1), .in2(OUT2), .in3(OUT3), .out(out_6), .sel(in_3));  // open: in0
  Register #(.width(4)) register_3 (.D(in_1), .en(ON3), .Q(OUT3), .clk(CLK), .clr(RST3));
  Clock clock_1 (.out(CLK));

  // Other names for the same wires on the sheet: AOUT[3:0] = out_5; BOUT[3:0] = out_6; DATA[3:0] = in_1;
  //   EA[1:0] = in_2; EB[1:0] = in_3; ERST[1:0] = in_4
endmodule
